// Logisim project Unidade 1_Capitulo 1 - Cofre Bancario.circ as structural Verilog: 1 circuit, main circuit main
module main (
  input  C,
  input  R,
  input  I,
  output A
);

  wire or_1_out;

  or or_1 (or_1_out, ~R, I);  // OR_Gate
  and and_1 (A, C, or_1_out);
endmodule
